// Logisim project Control Unit.circ as structural Verilog
module Control_Unit_2 (
  input  Start,
  input  Fetched,
  input  Halt_Instruction,
  input  Ejecutada,
  output out_5,
  output CS,
  output out_7
);

  wire demultiplexer_1_out0, demultiplexer_1_out1, demultiplexer_2_out0, demultiplexer_2_out1,
       demultiplexer_3_out0, demultiplexer_3_out1, demultiplexer_4_out0, demultiplexer_4_out1, undriven,
       undriven_2;

  Demultiplexer #(.enable("false")) demultiplexer_1 (
    .out0(demultiplexer_1_out0), .out1(demultiplexer_1_out1), .in(demultiplexer_1_out0), .sel(Start));
  or or_1 (out_5, demultiplexer_2_out0, demultiplexer_4_out1, demultiplexer_1_out1);
  Demultiplexer #(.enable("false")) demultiplexer_2 (
    .out0(demultiplexer_2_out0), .out1(demultiplexer_2_out1), .in(out_5));  // open: sel
  Demultiplexer #(.enable("false")) demultiplexer_3 (
    .out0(demultiplexer_3_out0), .out1(demultiplexer_3_out1), .in(demultiplexer_2_out1),
    .sel(Halt_Instruction));
  or or_2 (out_7, demultiplexer_4_out0, demultiplexer_3_out0);
  Demultiplexer demultiplexer_4 (
    .out0(demultiplexer_4_out0), .out1(demultiplexer_4_out1), .en(Ejecutada));  // open: in, sel
  or or_3 (CS, undriven, undriven_2);

  // Notes on the sheet:
  //   Iddle
  //   Capturar Instruccion
  //   Esquema de guia
  //   Execute
  //   Captura Instruccion
  //   Ejecuta Instruccion 
  //   End
endmodule
